// Logisim project lab6_1.circ as structural Verilog
module lab6_1 (
  input  s1,
  input  s0,
  input  in0,
  output \output ,
  output output2
);

  wire and_1_out, and_2_out, not_1_out, not_2_out;

  not not_1 (not_1_out, s1);
  not not_2 (not_2_out, in0);
  not not_3 (output2, s0);
  and and_1 (and_1_out, not_1_out, in0);
  and and_2 (and_2_out, s1, not_2_out);
  or or_1 (\output , and_1_out, and_2_out);
endmodule
