// Logisim project lab6_2.circ as structural Verilog
module lab6_2 (
  input  s2,
  input  s1,
  input  s0,
  input  in1,
  input  in0,
  output \output ,
  output output2,
  output output3
);

  wire and_1_out, and_2_out, and_3_out, and_4_out, and_5_out, and_6_out, and_7_out, not_1_out, not_2_out,
       not_3_out, not_4_out, not_5_out, not_6_out;

  and and_1 (and_1_out, s1, in0);
  and and_2 (and_2_out, s1, s0);
  not not_1 (not_1_out, s1);
  not not_2 (not_2_out, s1);
  not not_3 (not_3_out, s0);
  not not_4 (not_4_out, in0);
  not not_5 (not_5_out, s0);
  not not_6 (not_6_out, in0);
  or or_1 (\output , in1, and_1_out, and_2_out, s2);
  and and_3 (and_3_out, not_1_out, in0);
  and and_4 (and_4_out, not_2_out, s0);
  and and_5 (and_5_out, s1, not_3_out, not_4_out);
  and and_6 (and_6_out, not_5_out, not_6_out);
  and and_7 (and_7_out, s0, in0);
  or or_2 (output2, and_3_out, and_4_out, and_5_out);
  or or_3 (output3, and_6_out, and_7_out);
endmodule
